// Logisim project Practica1.circ as structural Verilog: 3 circuits, main circuit Ejercicio !
module Ejercicio (
  input  P,
  input  Q,
  output out_3
);

  wire not_1_out, not_2_out, or_1_out, or_2_out;

  not not_1 (not_1_out, P);
  not not_2 (not_2_out, Q);
  or or_1 (or_1_out, not_1_out, Q);
  or or_2 (or_2_out, not_2_out, P);
  and and_1 (out_3, or_1_out, or_2_out);

  // Notes on the sheet:
  //   Si y sólo si
endmodule

module Ejercicio_2 (
  input  A,
  input  B,
  input  C,
  output out_4
);

  wire and_1_out, and_2_out, and_3_out, and_4_out, not_1_out, not_2_out, not_3_out;

  not not_1 (not_1_out, A);
  not not_2 (not_2_out, B);
  not not_3 (not_3_out, C);
  and and_1 (and_1_out, not_1_out, not_2_out, not_3_out);
  and and_2 (and_2_out, A, B, not_3_out);
  and and_3 (and_3_out, not_2_out, A, C);
  and and_4 (and_4_out, B, C, not_1_out);
  or or_1 (out_4, and_1_out, and_2_out, and_3_out, and_4_out);

  // Notes on the sheet:
  //   Pares
endmodule

module Ejercicio_3 (
  input  A0,
  input  A1,
  input  A2,
  input  B0,
  input  B1,
  input  B2,
  output out_7
);

  wire not_1_out, not_2_out, not_3_out, not_4_out, not_5_out, not_6_out, or_1_out, or_2_out, or_3_out,
       or_4_out, or_5_out, or_6_out;

  not not_1 (not_1_out, A0);
  not not_2 (not_2_out, A1);
  not not_3 (not_3_out, A2);
  not not_4 (not_4_out, B0);
  not not_5 (not_5_out, B1);
  not not_6 (not_6_out, B2);
  or or_1 (or_1_out, not_1_out, B0);
  or or_2 (or_2_out, A0, not_4_out);
  or or_3 (or_3_out, not_2_out, B1);
  or or_4 (or_4_out, A1, not_5_out);
  or or_5 (or_5_out, not_3_out, B2);
  or or_6 (or_6_out, A2, not_6_out);
  and and_1 (out_7, or_1_out, or_2_out, or_3_out, or_4_out, or_5_out, or_6_out);

  // Notes on the sheet:
  //   x = y
endmodule
