// Logisim project CovaFelipePracticaL02.circ as structural Verilog: 2 circuits, main circuit A  mayor que B
module main (
  input  A,
  input  in_2,
  input  in_3,
  input  in_4,
  input  in_5,
  input  in_6,
  input  in_7,
  input  B,
  input  in_9,
  input  in_10,
  output A___B,
  output A___B_2,
  output A___B_3
);

  wire a_mayor_que_b_1_out_3, a_mayor_que_b_2_out_3, a_mayor_que_b_3_out_3, a_mayor_que_b_4_out_3,
       a_mayor_que_b_5_out_3, a_mayor_que_b_6_out_3, a_mayor_que_b_7_out_3, a_mayor_que_b_8_out_3,
       a_mayor_que_b_9_out_3, a_mayor_que_b_10_out_3, a_mayor_que_b_11_out_3, a_mayor_que_b_12_out_3,
       a_mayor_que_b_13_out_3, a_mayor_que_b_14_out_3, a_mayor_que_b_15_out_3, and_1_out, and_2_out,
       and_3_out, and_4_out, and_5_out, and_6_out, and_7_out, and_8_out, and_9_out, and_10_out, and_11_out,
       and_12_out, and_13_out, and_14_out, not_1_out, not_2_out, not_3_out, not_4_out, not_5_out, not_6_out,
       not_7_out, not_8_out, not_9_out, not_10_out, not_11_out, not_12_out, or_2_out, or_3_out, or_4_out,
       or_5_out, or_6_out;

  A__mayor_que_B a_mayor_que_b_1 (.A___1(A), .B___0(A), .out_3(a_mayor_que_b_1_out_3));
  A__mayor_que_B a_mayor_que_b_2 (.A___1(A), .B___0(A), .out_3(a_mayor_que_b_2_out_3));
  A__mayor_que_B a_mayor_que_b_3 (.A___1(in_2), .B___0(in_7), .out_3(a_mayor_que_b_3_out_3));
  A__mayor_que_B a_mayor_que_b_4 (.A___1(A), .B___0(A), .out_3(a_mayor_que_b_4_out_3));
  A__mayor_que_B a_mayor_que_b_5 (.A___1(in_2), .B___0(in_7), .out_3(a_mayor_que_b_5_out_3));
  A__mayor_que_B a_mayor_que_b_6 (.A___1(in_3), .B___0(B), .out_3(a_mayor_que_b_6_out_3));
  A__mayor_que_B a_mayor_que_b_7 (.A___1(A), .B___0(A), .out_3(a_mayor_que_b_7_out_3));
  A__mayor_que_B a_mayor_que_b_8 (.A___1(in_2), .B___0(in_7), .out_3(a_mayor_que_b_8_out_3));
  A__mayor_que_B a_mayor_que_b_9 (.A___1(in_3), .B___0(B), .out_3(a_mayor_que_b_9_out_3));
  A__mayor_que_B a_mayor_que_b_10 (.A___1(in_4), .B___0(in_9), .out_3(a_mayor_que_b_10_out_3));
  A__mayor_que_B a_mayor_que_b_11 (.A___1(in_5), .B___0(in_10), .out_3(a_mayor_que_b_11_out_3));
  A__mayor_que_B a_mayor_que_b_12 (.A___1(A), .B___0(A), .out_3(a_mayor_que_b_12_out_3));
  A__mayor_que_B a_mayor_que_b_13 (.A___1(in_2), .B___0(A), .out_3(a_mayor_que_b_13_out_3));
  A__mayor_que_B a_mayor_que_b_14 (.A___1(in_3), .B___0(in_7), .out_3(a_mayor_que_b_14_out_3));
  A__mayor_que_B a_mayor_que_b_15 (.A___1(in_4), .B___0(in_9), .out_3(a_mayor_que_b_15_out_3));
  not not_1 (not_1_out, A);
  not not_2 (not_2_out, A);
  not not_3 (not_3_out, in_2);
  not not_4 (not_4_out, in_7);
  not not_5 (not_5_out, in_3);
  not not_6 (not_6_out, B);
  not not_7 (not_7_out, in_4);
  not not_8 (not_8_out, in_9);
  not not_9 (not_9_out, in_5);
  not not_10 (not_10_out, in_10);
  and and_1 (and_1_out, a_mayor_que_b_2_out_3, a_mayor_que_b_3_out_3);
  and and_2 (and_2_out, a_mayor_que_b_4_out_3, a_mayor_que_b_6_out_3, a_mayor_que_b_5_out_3);
  and and_3 (and_3_out, a_mayor_que_b_7_out_3, a_mayor_que_b_8_out_3, a_mayor_que_b_10_out_3, a_mayor_que_b_9_out_3);
  and and_4 (and_4_out, a_mayor_que_b_12_out_3, a_mayor_que_b_11_out_3, a_mayor_que_b_13_out_3, a_mayor_que_b_14_out_3, a_mayor_que_b_15_out_3);
  and and_5 (and_5_out, A, A);
  and and_6 (and_6_out, not_1_out, not_2_out);
  and and_7 (and_7_out, in_7, in_2);
  and and_8 (and_8_out, not_3_out, not_4_out);
  and and_9 (and_9_out, B, in_3);
  and and_10 (and_10_out, not_5_out, not_6_out);
  and and_11 (and_11_out, in_9, in_4);
  and and_12 (and_12_out, not_7_out, not_8_out);
  and and_13 (and_13_out, in_10, in_5);
  and and_14 (and_14_out, not_9_out, not_10_out);
  or or_1 (A___B_3, a_mayor_que_b_1_out_3, and_1_out, and_2_out, and_3_out, and_4_out);
  or or_2 (or_2_out, and_5_out, and_6_out);
  or or_3 (or_3_out, and_7_out, and_8_out);
  or or_4 (or_4_out, and_9_out, and_10_out);
  or or_5 (or_5_out, and_11_out, and_12_out);
  or or_6 (or_6_out, and_13_out, and_14_out);
  and and_15 (A___B, or_2_out, or_3_out, or_4_out, or_5_out, or_6_out);
  not not_11 (not_11_out, A___B);
  not not_12 (not_12_out, A___B_3);
  and and_16 (A___B_2, not_11_out, not_12_out);

  assign in_6 = A;
endmodule

module A__mayor_que_B (
  input  A___1,
  input  B___0,
  output out_3
);

  wire not_1_out;

  not not_1 (not_1_out, B___0);
  and and_1 (out_3, A___1, not_1_out);
endmodule
