// Logisim project Practica3.circ as structural Verilog: 7 circuits, main circuit ALU 1 Bit
module ALU_8_Bits (
  input  [2:0] \Operación ,
  input  Acarreo_Entrada,
  input  [7:0] Byte_1,
  input  [7:0] Byte_2,
  output [7:0] Resultado,
  output Iguales,
  output Desbordamiento
);

  ALU_8_Bits_Subcircuito alu_8_bits_subcircuito_1 (
    .in_3(Byte_1), .in_4(Byte_2), .in_1(Acarreo_Entrada), .\Operación (\Operación ),
    .Desbordamiento(Desbordamiento), .Resultado(Resultado), .out_6(Iguales));
endmodule

module ALU_8_Bits_Subcircuito (
  input  in_1,
  input  [2:0] \Operación ,
  input  [7:0] in_3,
  input  [7:0] in_4,
  output [7:0] Resultado,
  output out_6,
  output Desbordamiento
);

  wire alu_1_bit_1_acarreo_salida, alu_1_bit_2_acarreo_salida, alu_1_bit_3_acarreo_salida,
       alu_1_bit_4_acarreo_salida, alu_1_bit_5_acarreo_salida, alu_1_bit_6_acarreo_salida,
       alu_1_bit_7_acarreo_salida, alu_1_bit_8_acarreo_salida, igualdad_8_bits_1_out_2, multiplexer_2_out,
       multiplexer_4_out, not_1_out;
  wire [7:0] c2_8bits_1_out_2, multiplexer_1_out;

  C2_8Bits c2_8bits_1 (.out_2(c2_8bits_1_out_2), .in_1(in_4));
  Multiplexer #(.select(3), .width(8)) multiplexer_1 (
    .in0(in_4), .in1(in_4), .in2(in_4), .in3(in_4), .in4(in_4), .in5(c2_8bits_1_out_2),
    .out(multiplexer_1_out), .sel(\Operación ));  // open: in6, in7, en
  // Probe on c2_8bits_1_out_2
  Multiplexer #(.select(3)) multiplexer_2 (
    .in0(1'b0), .in1(1'b0), .in2(1'b0), .in3(1'b0), .in4(in_1), .in5(1'b0), .out(multiplexer_2_out),
    .sel(\Operación ));  // open: in6, in7, en
  ALU_1_Bit alu_1_bit_1 (
    .Bit_1(in_3[0]), .Bit_2(multiplexer_1_out[0]), .Resultado(Resultado[0]), .CIn(multiplexer_2_out),
    .in_1(\Operación ), .Acarreo_Salida(alu_1_bit_1_acarreo_salida));
  ALU_1_Bit alu_1_bit_2 (
    .Bit_1(in_3[1]), .Bit_2(multiplexer_1_out[1]), .Resultado(Resultado[1]),
    .CIn(alu_1_bit_1_acarreo_salida), .in_1(\Operación ), .Acarreo_Salida(alu_1_bit_2_acarreo_salida));
  ALU_1_Bit alu_1_bit_3 (
    .Bit_1(in_3[2]), .Bit_2(multiplexer_1_out[2]), .Resultado(Resultado[2]),
    .CIn(alu_1_bit_2_acarreo_salida), .in_1(\Operación ), .Acarreo_Salida(alu_1_bit_3_acarreo_salida));
  ALU_1_Bit alu_1_bit_4 (
    .Bit_1(in_3[3]), .Bit_2(multiplexer_1_out[3]), .Resultado(Resultado[3]),
    .CIn(alu_1_bit_3_acarreo_salida), .in_1(\Operación ), .Acarreo_Salida(alu_1_bit_4_acarreo_salida));
  ALU_1_Bit alu_1_bit_5 (
    .Bit_1(in_3[4]), .Bit_2(multiplexer_1_out[4]), .Resultado(Resultado[4]),
    .CIn(alu_1_bit_4_acarreo_salida), .in_1(\Operación ), .Acarreo_Salida(alu_1_bit_5_acarreo_salida));
  ALU_1_Bit alu_1_bit_6 (
    .Bit_1(in_3[5]), .Bit_2(multiplexer_1_out[5]), .Resultado(Resultado[5]),
    .CIn(alu_1_bit_5_acarreo_salida), .in_1(\Operación ), .Acarreo_Salida(alu_1_bit_6_acarreo_salida));
  ALU_1_Bit alu_1_bit_7 (
    .Bit_1(in_3[6]), .Bit_2(multiplexer_1_out[6]), .Resultado(Resultado[6]),
    .CIn(alu_1_bit_6_acarreo_salida), .in_1(\Operación ), .Acarreo_Salida(alu_1_bit_7_acarreo_salida));
  ALU_1_Bit alu_1_bit_8 (
    .Bit_1(in_3[7]), .Bit_2(multiplexer_1_out[7]), .Resultado(Resultado[7]),
    .CIn(alu_1_bit_7_acarreo_salida), .in_1(\Operación ), .Acarreo_Salida(alu_1_bit_8_acarreo_salida));
  not not_1 (not_1_out, alu_1_bit_8_acarreo_salida);
  Multiplexer #(.select(3)) multiplexer_3 (
    .in0(1'b0), .in1(1'b0), .in2(1'b0), .in3(1'b0), .in4(alu_1_bit_8_acarreo_salida), .in5(not_1_out),
    .out(Desbordamiento), .sel(\Operación ));  // open: in6, in7, en
  Igualdad_8_Bits igualdad_8_bits_1 (.in_1(Resultado), .out_2(igualdad_8_bits_1_out_2));
  and and_1 (out_6, igualdad_8_bits_1_out_2, multiplexer_4_out);
  Multiplexer #(.select(3)) multiplexer_4 (
    .in0(1'b0), .in1(1'b0), .in2(1'b0), .in3(1'b1), .in4(1'b0), .in5(1'b0), .out(multiplexer_4_out),
    .sel(\Operación ));  // open: in6, in7, en

  // Notes on the sheet:
  //   Si la operación no es suma
  //   el desbordamiento es 0
  //   Para la Resta, si el 2do
  //   número es mayor al 1ero
  //   => se saca complemento
  //   a dos del resultado.
  //   Si el número es 1,
  //   Los números son
  //   iguales
endmodule

module ALU_1_Bit (
  input  [2:0] in_1,
  input  CIn,
  input  Bit_1,
  input  Bit_2,
  output Resultado,
  output Acarreo_Salida
);

  wire n_PvQ_out, not_1_out, P___Q_out, P_v_Q_out, sumador_1_bit_1_a_b, xor_1_out_3;

  and P___Q (P___Q_out, Bit_1, Bit_2);
  or P_v_Q (P_v_Q_out, Bit_1, Bit_2);
  not not_1 (not_1_out, xor_1_out_3);
  nor n_PvQ (n_PvQ_out, Bit_1, Bit_2);
  XOR xor_1 (.in_1(Bit_1), .in_2(Bit_2), .out_3(xor_1_out_3));
  Sumador_1_Bit sumador_1_bit_1 (
    .in_1(Bit_1), .in_3(Bit_2), .A_B(sumador_1_bit_1_a_b), .CIn(CIn), .COut(Acarreo_Salida));
  Multiplexer #(.select(3)) multiplexer_1 (
    .in0(P___Q_out), .in1(P_v_Q_out), .in2(n_PvQ_out), .in3(not_1_out), .in4(sumador_1_bit_1_a_b),
    .in5(sumador_1_bit_1_a_b), .out(Resultado), .sel(in_1));  // open: in6, in7, en
endmodule

module C2_8Bits (
  input  [7:0] in_1,
  output [7:0] out_2
);

  wire sumador_1_bit_1_cout, sumador_1_bit_2_cout, sumador_1_bit_3_cout, sumador_1_bit_4_cout,
       sumador_1_bit_5_cout, sumador_1_bit_6_cout, sumador_1_bit_7_cout, sumador_1_bit_8_cout;
  wire [7:0] not_1_out;

  assign not_1_out = ~in_1;  // NOT_Gate not_1, 8 bits wide
  Sumador_1_Bit sumador_1_bit_1 (
    .in_1(not_1_out[0]), .in_3(1'b1), .A_B(out_2[0]), .CIn(1'b0), .COut(sumador_1_bit_1_cout));
  Sumador_1_Bit sumador_1_bit_2 (
    .in_1(not_1_out[1]), .in_3(1'b0), .A_B(out_2[1]), .CIn(sumador_1_bit_1_cout), .COut(sumador_1_bit_2_cout));
  Sumador_1_Bit sumador_1_bit_3 (
    .in_1(not_1_out[2]), .in_3(1'b0), .A_B(out_2[2]), .CIn(sumador_1_bit_2_cout), .COut(sumador_1_bit_3_cout));
  Sumador_1_Bit sumador_1_bit_4 (
    .in_1(not_1_out[3]), .in_3(1'b0), .A_B(out_2[3]), .CIn(sumador_1_bit_3_cout), .COut(sumador_1_bit_4_cout));
  Sumador_1_Bit sumador_1_bit_5 (
    .in_1(not_1_out[4]), .in_3(1'b0), .A_B(out_2[4]), .CIn(sumador_1_bit_4_cout), .COut(sumador_1_bit_5_cout));
  Sumador_1_Bit sumador_1_bit_6 (
    .in_1(not_1_out[5]), .in_3(1'b0), .A_B(out_2[5]), .CIn(sumador_1_bit_5_cout), .COut(sumador_1_bit_6_cout));
  Sumador_1_Bit sumador_1_bit_7 (
    .in_1(not_1_out[6]), .in_3(1'b0), .A_B(out_2[6]), .CIn(sumador_1_bit_6_cout), .COut(sumador_1_bit_7_cout));
  Sumador_1_Bit sumador_1_bit_8 (
    .in_1(not_1_out[7]), .in_3(1'b0), .A_B(out_2[7]), .CIn(sumador_1_bit_7_cout), .COut(sumador_1_bit_8_cout));
  // Probe on sumador_1_bit_8_cout
endmodule

module Igualdad_8_Bits (
  input  [7:0] in_1,
  output out_2
);

  and and_1 (out_2, in_1[7], in_1[6], in_1[5], in_1[4], in_1[3], in_1[2], in_1[1], in_1[0]);
endmodule

module Sumador_1_Bit (
  input  in_1,
  input  CIn,
  input  in_3,
  output A_B,
  output COut
);

  wire and_1_out, and_2_out, xor_1_out_3;

  and and_1 (and_1_out, in_1, in_3);
  XOR xor_1 (.in_1(in_1), .in_2(in_3), .out_3(xor_1_out_3));
  and and_2 (and_2_out, xor_1_out_3, CIn);
  or or_1 (COut, and_1_out, and_2_out);
  XOR xor_2 (.in_1(CIn), .in_2(xor_1_out_3), .out_3(A_B));
endmodule

module XOR (
  input  in_1,
  input  in_2,
  output out_3
);

  wire not_1_out, not_2_out, or_1_out, or_2_out;

  not not_1 (not_1_out, in_1);
  not not_2 (not_2_out, in_2);
  or or_1 (or_1_out, in_1, in_2);
  or or_2 (or_2_out, not_1_out, not_2_out);
  and and_1 (out_3, or_1_out, or_2_out);
endmodule
